// Logisim project test_circuit.circ as structural Verilog: 1 circuit, main circuit main
module main (
  output [15:0] r0,
  output [15:0] r1,
  output [15:0] r2,
  output [15:0] r3,
  output [15:0] r4,
  output [15:0] r5,
  output [15:0] r6,
  output [15:0] r7,
  output [15:0] fp,
  output [15:0] pc,
  output [15:0] sp,
  output [15:0] ps,
  output halt
);

  wire cdm16_1_data_ins_prime, cdm16_1_mem, cdm16_1_rd_wr_prime, cdm16_1_word, clock_1_out, decoder_2_out0,
       decoder_2_out1, not_1_out;
  wire [1:0] cdm16_1_status;
  wire [15:0] cdm16_1_address, cdm16_1_data_out, controlled_buffer_1_out, controlled_buffer_2_out;

  Clock clock_1 (.out(clock_1_out));
  cdm16 cdm16_1 (
    .mem(cdm16_1_mem), .data_ins_prime(cdm16_1_data_ins_prime), .rd_wr_prime(cdm16_1_rd_wr_prime),
    .address(cdm16_1_address), .word(cdm16_1_word), .R0(r0), .R1(r1), .R2(r2), .R3(r3), .R4(r4), .R5(r5),
    .R6(r6), .FP(fp), .PC(pc), .PS(ps), .SP(sp), .status(cdm16_1_status), .data_out(cdm16_1_data_out),
    .data_in(controlled_buffer_2_out), .clock(clock_1_out));  // open: EXC, exc_vec, IRQ, int_vec, hold, IAck, fetch
  Decoder #(.select(2), .enable("false")) decoder_1 (.out2(halt), .sel(cdm16_1_status));  // open: out0, out1, out3
  Decoder #(.disabled(0)) decoder_2 (
    .out0(decoder_2_out0), .out1(decoder_2_out1), .sel(cdm16_1_data_ins_prime), .en(cdm16_1_mem));
  not not_1 (not_1_out, cdm16_1_rd_wr_prime);
  assign controlled_buffer_1_out = not_1_out ? cdm16_1_data_out : 16'bz;  // Controlled_Buffer controlled_buffer_1
  assign controlled_buffer_2_out = cdm16_1_rd_wr_prime ? controlled_buffer_1_out : 16'bz;  // Controlled_Buffer controlled_buffer_2
  // ROM rom_1: pin names not known; wires that end beside it: cdm16_1_address, decoder_2_out0, cdm16_1_word, controlled_buffer_1_out
  // RAM ram_1: pin names not known; wires that end beside it: cdm16_1_address, cdm16_1_word, decoder_2_out1, clock_1_out, cdm16_1_rd_wr_prime, controlled_buffer_1_out

  assign r7 = fp;
endmodule
