// Logisim project test_circuit.circ as structural Verilog: 1 circuit, main circuit main
module main (
  output [7:0] r0,
  output [7:0] r1,
  output [7:0] r2,
  output [7:0] r3,
  output [7:0] pc,
  output [7:0] sp,
  output [7:0] ps,
  output halt
);

  wire cdm_8_mark5_1_data_inst, cdm_8_mark5_1_mem_cycle, cdm_8_mark5_1_mem_read, clock_1_out,
       comparator_1_eq, data, data_io, decoder_1_out0, not_1_out, \reg ;
  wire [7:0] cdm_8_mark5_1_addr, cdm_8_mark5_1_data_out, controlled_buffer_1_out, controlled_buffer_2_out;
  wire [7:1] register_1_q;
  wire [15:8] pull_resistor_1_node, pull_resistor_2_node;

  Clock clock_1 (.out(clock_1_out));
  CdM_8_mark5 cdm_8_mark5_1 (
    .clock(clock_1_out), .addr(cdm_8_mark5_1_addr), .mem_read(cdm_8_mark5_1_mem_read),
    .mem_cycle(cdm_8_mark5_1_mem_cycle), .data_inst(cdm_8_mark5_1_data_inst),
    .data_out(cdm_8_mark5_1_data_out), .data_in(controlled_buffer_2_out), .r0(r0), .r1(r1), .r2(r2), .r3(r3),
    .PC(pc), .SP(sp), .PS(ps));  // open: IAck, IRQ, vec
  Decoder #(.disabled(0)) decoder_1 (
    .out0(decoder_1_out0), .out1(data_io), .sel(cdm_8_mark5_1_data_inst), .en(cdm_8_mark5_1_mem_cycle));
  not not_1 (not_1_out, cdm_8_mark5_1_mem_read);
  assign controlled_buffer_1_out = not_1_out ? cdm_8_mark5_1_data_out : 8'bz;  // Controlled_Buffer controlled_buffer_1
  assign controlled_buffer_2_out = cdm_8_mark5_1_mem_read ? controlled_buffer_1_out : 8'bz;  // Controlled_Buffer controlled_buffer_2
  Decoder #(.disabled(0)) decoder_2 (.out0(data), .out1(\reg ), .sel(comparator_1_eq), .en(data_io));
  Comparator comparator_1 (.a(cdm_8_mark5_1_addr), .b({8{1'b1}}), .eq(comparator_1_eq));  // open: gt, lt
  Pull_Resistor pull_resistor_1 (.node(pull_resistor_1_node));
  // ROM rom_1: pin names not known; wires that end beside it: cdm_8_mark5_1_addr, decoder_1_out0, {pull_resistor_1_node, controlled_buffer_1_out}
  Pull_Resistor pull_resistor_2 (.node(pull_resistor_2_node));
  // RAM ram_1: pin names not known; wires that end beside it: cdm_8_mark5_1_addr, data, clock_1_out, cdm_8_mark5_1_mem_read, {pull_resistor_2_node, controlled_buffer_1_out}
  Register register_1 (
    .D(controlled_buffer_1_out), .en(\reg ), .Q({register_1_q, halt}), .clk(clock_1_out));  // open: clr
endmodule
