// Logisim project test_circuit.circ as structural Verilog: 1 circuit, main circuit main
module main (
  output [7:0] r0,
  output [7:0] r1,
  output [7:0] r2,
  output [7:0] r3,
  output [15:0] pc,
  output [7:0] sp,
  output [7:0] ps,
  output halt
);

  wire cdm_8e_1_data_inst, cdm_8e_1_mem_cycle, cdm_8e_1_mem_read, clock_1_out, decoder_1_out0,
       decoder_1_out1, not_1_out;
  wire [7:0] cdm_8e_1_data_out, controlled_buffer_1_out, controlled_buffer_2_out;
  wire [15:0] cdm_8e_1_addr;
  wire [15:8] pull_resistor_2_node, rom_1_p3;

  Clock clock_1 (.out(clock_1_out));
  CdM_8e cdm_8e_1 (
    .clock(clock_1_out), .addr(cdm_8e_1_addr), .mem_read(cdm_8e_1_mem_read), .mem_cycle(cdm_8e_1_mem_cycle),
    .data_inst(cdm_8e_1_data_inst), .data_out(cdm_8e_1_data_out), .data_in(controlled_buffer_2_out), .r0(r0),
    .r1(r1), .r2(r2), .r3(r3), .PC(pc), .SP(sp), .PS(ps), .halted(halt));  // open: IAck, IRQ, vec
  Decoder #(.disabled(0)) decoder_1 (
    .out0(decoder_1_out0), .out1(decoder_1_out1), .sel(cdm_8e_1_data_inst), .en(cdm_8e_1_mem_cycle));
  not not_1 (not_1_out, cdm_8e_1_mem_read);
  assign controlled_buffer_1_out = not_1_out ? cdm_8e_1_data_out : 8'bz;  // Controlled_Buffer controlled_buffer_1
  assign controlled_buffer_2_out = cdm_8e_1_mem_read ? controlled_buffer_1_out : 8'bz;  // Controlled_Buffer controlled_buffer_2
  // ROM rom_1: pin names not known; wires that end beside it: cdm_8e_1_addr, decoder_1_out0, {rom_1_p3, controlled_buffer_1_out}
  Pull_Resistor pull_resistor_1 (.node(rom_1_p3));
  Pull_Resistor pull_resistor_2 (.node(pull_resistor_2_node));
  // RAM ram_1: pin names not known; wires that end beside it: cdm_8e_1_addr[7:0], decoder_1_out1, clock_1_out, cdm_8e_1_mem_read, {pull_resistor_2_node, controlled_buffer_1_out}
endmodule
